// Logisim project CPUMk1.circ as structural Verilog
module ALU (
  input  [2:0] Operation_Select,
  input  [15:0] Input_A,
  input  [15:0] Input_B,
  output [15:0] Outut_B
);

  wire [15:0] adder_1_out, adder_2_out, adder_3_out, and_1_out, or_1_out, subtractor_1_out;

  Adder #(.width(16)) adder_1 (.a(Input_A), .b(16'h1), .out(adder_1_out));  // open: cin, cout
  Adder #(.width(16)) adder_2 (.a(Input_B), .b(16'h1), .out(adder_2_out));  // open: cin, cout
  Adder #(.width(16)) adder_3 (.a(Input_A), .b(Input_B), .out(adder_3_out));  // open: cin, cout
  Subtractor #(.width(16)) subtractor_1 (.a(Input_A), .b(Input_B), .out(subtractor_1_out));  // open: bin, bout
  assign and_1_out = Input_A & Input_B;  // AND_Gate and_1, 16 bits wide
  assign or_1_out = Input_A | Input_B;  // OR_Gate or_1, 16 bits wide
  Multiplexer #(.select(3), .width(16)) multiplexer_1 (
    .in0(Input_A), .in1(Input_B), .in2(and_1_out), .in3(or_1_out), .in4(adder_1_out), .in5(adder_2_out),
    .in6(adder_3_out), .in7(subtractor_1_out), .out(Outut_B), .sel(Operation_Select));  // open: en
endmodule

module CPU (
  input  [15:0] Ext_input,
  input  [15:0] Mem_input,
  output [15:0] Memory_Selector,
  output [15:0] out_4,
  output [15:0] out_5,
  output [2:0] out_6,
  output [1:0] out_7,
  output [15:0] Output,
  output [17:0] out_9
);

  wire CLK;
  wire [6:0] MPC_q, multiplexer_2_out;
  wire [15:0] A_q, B_q, Mem_q;

  Clock clock_1 (.out(CLK));
  Register #(.width(16)) IC (.D(out_5), .Q(Memory_Selector), .clk(out_9[13]));  // open: en, clr
  Register #(.width(16)) A (.D(out_5), .Q(A_q), .clk(out_9[14]));  // open: en, clr
  Register #(.width(16)) B (.D(out_5), .Q(B_q), .clk(out_9[15]));  // open: en, clr
  Register #(.width(16)) Out (.D(out_5), .Q(Output), .clk(out_9[16]));  // open: en, clr
  Register #(.width(16)) Mem (.D(Mem_input), .Q(Mem_q), .clk(out_9[17]));  // open: en, clr
  Multiplexer #(.select(2), .width(16)) multiplexer_1 (
    .in0(B_q), .in1(Mem_q), .in2(Memory_Selector), .in3(Ext_input), .out(out_4), .sel(out_7));  // open: en
  ALU alu_1 (.Operation_Select(out_6), .Input_A(A_q), .Input_B(out_4), .Outut_B(out_5));
  Multiplexer #(.width(7)) multiplexer_2 (
    .in0(Mem_q[6:0]), .in1(out_9[6:0]), .out(multiplexer_2_out), .sel(out_9[7]));  // open: en
  Register #(.width(7)) MPC (.D(multiplexer_2_out), .Q(MPC_q), .clk(CLK));  // open: en, clr
  ROM #(.addrWidth(7), .dataWidth(18)) rom_1 (
    .addr(MPC_q), .data({out_9[17:13], out_7, out_6, out_9[7:0]}));  // open: sel

  assign out_9[12:8] = {out_7, out_6};

  // Other names for the same wires on the sheet: ALU_Control[2:0] = out_6; Write_IC = out_9[13]; Write_A = out_9[14];
  //   Write_B = out_9[15]; Write_Out = out_9[16]; Write_Mem = out_9[17]

  // Notes on the sheet:
  //   contents of rom_1 (hex, n*v repeats v):
  //   1581 3582 20000 84 8080 186 4180 1588 3589 2098a 4980
endmodule
